// Logisim project Tarea_C3B_inspeccion_calidad.circ as structural Verilog: 7 circuits, main circuit a_moore_bloques
module a_moore_bloques (
  input  CLK,
  input  P,
  output E0,
  output E1
);

  wire S0, S1, S2;
  wire [2:0] a_moore_next_state_1_s_n;

  a_moore_next_state a_moore_next_state_1 (.S({S2, S1, S0}), .P(P), .S_n(a_moore_next_state_1_s_n));
  D_Flip_Flop d_ff_1 (.D(a_moore_next_state_1_s_n[0]), .clk(CLK), .Q(S0));  // open: Qn, preset, reset
  D_Flip_Flop d_ff_2 (.D(a_moore_next_state_1_s_n[1]), .clk(CLK), .Q(S1));  // open: Qn, preset, reset
  D_Flip_Flop d_ff_3 (.D(a_moore_next_state_1_s_n[2]), .clk(CLK), .Q(S2));  // open: Qn, preset, reset
  a_moore_output_logic a_moore_output_logic_1 (.S({S2, S1, S0}), .E({E1, E0}));

  // Notes on the sheet:
  //   SALIDA E
  //   00=avanzar
  //   10=rechazado
  //   01=aceptado
endmodule

module a_moore_next_state (
  input  [2:0] S,
  input  P,
  output [2:0] S_n
);

  wire and_2_out, and_3_out, and_4_out, and_5_out, and_6_out, not_1_out, not_2_out, not_3_out, not_4_out;

  not not_1 (not_1_out, S[2]);
  not not_2 (not_2_out, S[1]);
  not not_3 (not_3_out, S[0]);
  not not_4 (not_4_out, P);
  and and_1 (S_n[2], S[1], not_3_out, P);
  and and_2 (and_2_out, not_2_out, S[0]);
  and and_3 (and_3_out, S[1], not_3_out, not_4_out);
  and and_4 (and_4_out, not_1_out, not_2_out, not_3_out, P);
  and and_5 (and_5_out, not_2_out, S[0], not_4_out);
  and and_6 (and_6_out, S[1], not_3_out, not_4_out);
  or or_1 (S_n[1], and_2_out, and_3_out);
  or or_2 (S_n[0], and_4_out, and_5_out, and_6_out);
endmodule

module a_moore_output_logic (
  input  [2:0] S,
  output [1:0] E
);

  and and_1 (E[0], S[1], S[0]);

  assign E[1] = S[2];
endmodule

module b_mealy_next_state_banda (
  input  S0,
  input  S1,
  input  E0,
  input  E1,
  input  K,
  output S_n0,
  output S_n1
);

  wire and_1_out, and_2_out, and_3_out, and_4_out, not_1_out, not_2_out, not_3_out;

  not not_1 (not_1_out, S0);
  not not_2 (not_2_out, E0);
  not not_3 (not_3_out, E1);
  and and_1 (and_1_out, not_1_out, not_2_out, E1, K);
  and and_2 (and_2_out, not_1_out, E0, not_3_out, K);
  and and_3 (and_3_out, not_1_out, not_2_out, K);
  and and_4 (and_4_out, not_1_out, E1, K);
  or or_1 (S_n0, and_1_out, and_2_out);
  or or_2 (S_n1, and_3_out, and_4_out);
endmodule

module b_mealy_output_logic (
  input  S0,
  input  S1,
  input  E0,
  input  E1,
  input  K,
  output B,
  output P0,
  output P1
);

  wire and_1_out, and_2_out, and_3_out, and_4_out, not_1_out, not_2_out, not_3_out, not_4_out;

  not not_1 (not_1_out, S0);
  not not_2 (not_2_out, S1);
  not not_3 (not_3_out, E0);
  not not_4 (not_4_out, E1);
  or or_1 (B, K, E1, E0, S0);
  and and_1 (and_1_out, not_1_out, not_2_out, E0, not_4_out, K);
  and and_2 (and_2_out, not_1_out, S1, E0, not_4_out, K);
  and and_3 (and_3_out, not_1_out, not_2_out, not_3_out, E1, K);
  and and_4 (and_4_out, not_1_out, S1, not_3_out, E1, K);
  or or_2 (P0, and_1_out, and_2_out);
  or or_3 (P1, and_3_out, and_4_out);
endmodule

module b_mealy_bloque (
  input  CLK,
  input  E0,
  input  E1,
  input  K,
  output B,
  output P0,
  output P1
);

  wire b_mealy_next_state_banda_1_s_n0, b_mealy_next_state_banda_1_s_n1, S0, S1;

  b_mealy_next_state_banda b_mealy_next_state_banda_1 (
    .S0(S0), .S1(S1), .E0(E0), .E1(E1), .K(K), .S_n0(b_mealy_next_state_banda_1_s_n0),
    .S_n1(b_mealy_next_state_banda_1_s_n1));
  D_Flip_Flop d_ff_1 (.D(b_mealy_next_state_banda_1_s_n0), .clk(CLK), .Q(S0));  // open: Qn, preset, reset
  D_Flip_Flop d_ff_2 (.D(b_mealy_next_state_banda_1_s_n1), .clk(CLK), .Q(S1));  // open: Qn, preset, reset
  b_mealy_output_logic b_mealy_output_logic_1 (.S0(S0), .S1(S1), .E0(E0), .E1(E1), .K(K), .B(B), .P0(P0), .P1(P1));

  // Notes on the sheet:
  //   SALIDA P
  //   00=nada
  //   10=rechazado
  //   01=aceptado
endmodule

module a_b_inspeccion_producto (
  input  CLK,
  input  PRODUCTO,
  input  ON_OFF,
  output BANDA_TRANSPORTADORA,
  output P0,
  output P1
);

  wire a_moore_bloques_1_e0, a_moore_bloques_1_e1;

  a_moore_bloques a_moore_bloques_1 (.CLK(CLK), .P(PRODUCTO), .E0(a_moore_bloques_1_e0), .E1(a_moore_bloques_1_e1));
  b_mealy_bloque b_mealy_bloque_1 (
    .CLK(CLK), .E0(a_moore_bloques_1_e0), .E1(a_moore_bloques_1_e1), .K(ON_OFF), .B(BANDA_TRANSPORTADORA),
    .P0(P0), .P1(P1));

  // Notes on the sheet:
  //   SALIDA P
  //   00=nada
  //   10=rechazado
  //   01=aceptado
endmodule
